# Fritzing sketch display_minimal (saved by Fritzing 0.9.3b)
circuit board: 7.5cm x 10cm
breadboards: 1

parts:
  LED_A_D1 = LED - 5mm [color="Red (633nm)" package="5 mm [THT]"]
  LED_K_D1 = LED - 5mm [color="Red (633nm)" package="5 mm [THT]"]
  LED_B_D1 = LED - 5mm [color="Red (633nm)" package="5 mm [THT]"]
  LED_E_D1 = LED - 5mm [color="Red (633nm)" package="5 mm [THT]"]
  LED_G_D1 = LED - 5mm [color="Red (633nm)" package="5 mm [THT]"]
  LED_H_D1 = LED - 5mm [color="Red (633nm)" package="5 mm [THT]"]
  LED_N_D1 = LED - 5mm [color="Red (633nm)" package="5 mm [THT]"]
  LED_L_D1 = LED - 5mm [color="Red (633nm)" package="5 mm [THT]"]
  LED_D_D1 = LED - 5mm [color="Red (633nm)" package="5 mm [THT]"]
  LED_F_D1 = LED - 5mm [color="Red (633nm)" package="5 mm [THT]"]
  LED_I_D1 = LED - 5mm [color="Red (633nm)" package="5 mm [THT]"]
  LED_J_D1 = LED - 5mm [color="Red (633nm)" package="5 mm [THT]"]
  LED_C_D1 = LED - 5mm [color="Red (633nm)" package="5 mm [THT]"]
  LED_M_D1 = LED - 5mm [color="Red (633nm)" package="5 mm [THT]"]
  RA = Resistor [tolerance=±5% resistance=120 package=THT]
  RK = Resistor [tolerance=±5% resistance=120 package=THT]
  RM = Resistor [tolerance=±5% resistance=120 package=THT]
  RN = Resistor [tolerance=±5% resistance=120 package=THT]
  RG = Resistor [tolerance=±5% resistance=120 package=THT]
  RL = Resistor [tolerance=±5% resistance=120 package=THT]
  RI = Resistor [tolerance=±5% resistance=120 package=THT]
  RC = Resistor [tolerance=±5% resistance=120 power=125mW package=THT]
  RF = Resistor [tolerance=±5% resistance=120 package=THT]
  RB = Resistor [tolerance=±5% resistance=120 package=THT]
  RJ = Resistor [tolerance=±5% resistance=120 package=THT]
  RH = Resistor [tolerance=±5% resistance=120 package=THT]
  RE = Resistor [tolerance=±5% resistance=120 package=THT]
  RD = Resistor [tolerance=±5% resistance=120 package=THT]
  Segments = female pin header, 16 pins [form="♀ (female)"]
  Segments1 = female pin header, 15 pins [form="♀ (female)"]

nets:
  N1: LED_A_D1.cathode, LED_K_D1.cathode, LED_B_D1.cathode, LED_E_D1.cathode, LED_G_D1.cathode, LED_H_D1.cathode, LED_N_D1.cathode, LED_L_D1.cathode, LED_D_D1.cathode, LED_F_D1.cathode, LED_I_D1.cathode, LED_J_D1.cathode, LED_C_D1.cathode, LED_M_D1.cathode, Segments.pin16
  N2: LED_A_D1.anode, RA.Pin_1
  N3: LED_K_D1.anode, RK.Pin_1
  N4: LED_B_D1.anode, RB.Pin_1
  N5: LED_E_D1.anode, RE.Pin_1
  N6: LED_G_D1.anode, RG.Pin_1
  N7: LED_H_D1.anode, RH.Pin_1
  N8: LED_N_D1.anode, RN.Pin_1
  N9: LED_L_D1.anode, RL.Pin_1
  N10: LED_D_D1.anode, RD.Pin_1
  N11: LED_F_D1.anode, RF.Pin_1
  N12: LED_I_D1.anode, RI.Pin_1
  N13: LED_J_D1.anode, RJ.Pin_1
  N14: LED_C_D1.anode, RC.Pin_1
  N15: LED_M_D1.anode, RM.Pin_1
  sA: RA.Pin_0, Segments.pin1, Segments1.pin1
  sK: RK.Pin_0, Segments.pin5, Segments1.pin5
  sM: RM.Pin_0, Segments.pin11, Segments1.pin11
  sL: RN.Pin_0, Segments.pin12, Segments1.pin12
  sH: RG.Pin_0, Segments.pin7, Segments1.pin7
  sN: RL.Pin_0, Segments.pin10, Segments1.pin10
  sJ: RI.Pin_0, Segments.pin4, Segments1.pin4
  sE: RC.Pin_0, Segments.pin13, Segments1.pin13
  sI: RF.Pin_0, Segments.pin3, Segments1.pin3
  sB: RB.Pin_0, Segments.pin6, Segments1.pin6
  sF: RJ.Pin_0, Segments.pin2, Segments1.pin2
  sG: RH.Pin_0, Segments.pin8, Segments1.pin8
  sC: RE.Pin_0, Segments.pin9, Segments1.pin9
  sD: RD.Pin_0, Segments.pin14, Segments1.pin14
  s:: Segments.pin15, Segments1.pin15

notes:
  These inputs should come from a 5V-based microcontroller (untested with 3.3V or others)
