# Fritzing sketch isolated_display (saved by Fritzing 0.9.3b)
circuit board: 7.5cm x 10cm
breadboards: 1

parts:
  LED_A_D1 = LED - 5mm [color="Red (633nm)" package="5 mm [THT]"]
  LED_K_D1 = LED - 5mm [color="Red (633nm)" package="5 mm [THT]"]
  LED_B_D1 = LED - 5mm [color="Red (633nm)" package="5 mm [THT]"]
  LED_E_D1 = LED - 5mm [color="Red (633nm)" package="5 mm [THT]"]
  LED_G_D1 = LED - 5mm [color="Red (633nm)" package="5 mm [THT]"]
  LED_H_D1 = LED - 5mm [color="Red (633nm)" package="5 mm [THT]"]
  LED_N_D1 = LED - 5mm [color="Red (633nm)" package="5 mm [THT]"]
  LED_L_D1 = LED - 5mm [color="Red (633nm)" package="5 mm [THT]"]
  LED_D_D1 = LED - 5mm [color="Red (633nm)" package="5 mm [THT]"]
  LED_F_D1 = LED - 5mm [color="Red (633nm)" package="5 mm [THT]"]
  LED_I_D1 = LED - 5mm [color="Red (633nm)" package="5 mm [THT]"]
  LED_J_D1 = LED - 5mm [color="Red (633nm)" package="5 mm [THT]"]
  LED_C_D1 = LED - 5mm [color="Red (633nm)" package="5 mm [THT]"]
  LED_M_D1 = LED - 5mm [color="Red (633nm)" package="5 mm [THT]"]
  RA = Resistor [tolerance=±5% resistance=120 package=THT]
  RK = Resistor [tolerance=±5% resistance=120 package=THT]
  RM = Resistor [tolerance=±5% resistance=120 package=THT]
  RN = Resistor [tolerance=±5% resistance=120 package=THT]
  RG = Resistor [tolerance=±5% resistance=120 package=THT]
  RL = Resistor [tolerance=±5% resistance=120 package=THT]
  RI = Resistor [tolerance=±5% resistance=120 package=THT]
  RC = Resistor [tolerance=±5% resistance=120 power=125mW package=THT]
  RF = Resistor [tolerance=±5% resistance=120 package=THT]
  RB = Resistor [tolerance=±5% resistance=120 package=THT]
  RJ = Resistor [tolerance=±5% resistance=120 package=THT]
  RH = Resistor [tolerance=±5% resistance=120 package=THT]
  RE = Resistor [tolerance=±5% resistance=120 package=THT]
  RD = Resistor [tolerance=±5% resistance=120 package=THT]
  QA = NPN-Transistor [package="TO92 [THT]"]
  QK = NPN-Transistor [package="TO92 [THT]"]
  QI = NPN-Transistor [package="TO92 [THT]"]
  QF = NPN-Transistor [package="TO92 [THT]"]
  QC = NPN-Transistor [package="TO92 [THT]"]
  QB = NPN-Transistor [package="TO92 [THT]"]
  QH = NPN-Transistor [package="TO92 [THT]"]
  QN = NPN-Transistor [package="TO92 [THT]"]
  QL = NPN-Transistor [package="TO92 [THT]"]
  QE = NPN-Transistor [package="TO92 [THT]"]
  QD = NPN-Transistor [package="TO92 [THT]"]
  QJ = NPN-Transistor [package="TO92 [THT]"]
  QG = NPN-Transistor [package="TO92 [THT]"]
  QM = NPN-Transistor [package="TO92 [THT]"]
  RAQ = Resistor [tolerance=±5% resistance=30k package=THT]
  RFQ = Resistor [tolerance=±5% resistance=30k package=THT]
  RMQ = Resistor [tolerance=±5% resistance=30k package=THT]
  RCQ = Resistor [tolerance=±5% resistance=30k package=THT]
  RBQ = Resistor [tolerance=±5% resistance=30k package=THT]
  RJQ = Resistor [tolerance=±5% resistance=30k package=THT]
  REQ = Resistor [tolerance=±5% resistance=30k package=THT]
  RKQ = Resistor [tolerance=±5% resistance=30k package=THT]
  RGQ = Resistor [tolerance=±5% resistance=30k package=THT]
  RHQ = Resistor [tolerance=±5% resistance=30k package=THT]
  RIQ = Resistor [tolerance=±5% resistance=30k package=THT]
  RLQ = Resistor [tolerance=±5% resistance=30k package=THT]
  Qout = NPN-Transistor [package="TO92 [THT]"]
  RoutQ = Resistor [tolerance=±5% resistance=10k package=THT]
  RDQ = Resistor [tolerance=±5% resistance=30k package=THT]
  LED__up = LED - 5mm [color="Red (633nm)" package="5 mm [THT]"]
  R_up = Resistor [tolerance=±5% resistance=120 package=THT]
  Q = NPN-Transistor [package="TO92 [THT]"]
  R_Q = Resistor [tolerance=±5% resistance=30k package=THT]
  R_down = Resistor [tolerance=±5% resistance=120 package=THT]
  LED__down = LED - 5mm [color="Red (633nm)" package="5 mm [THT]"]
  RNQ = Resistor [tolerance=±5% resistance=30k package=THT]
  Power = Screw terminal - 2 pins [package=THT]
  Segments = female pin header, 15 pins [form="♀ (female)"]
  select = female pin header, 1 pin [form="♀ (female)"]

nets:
  N1: LED_A_D1.cathode, QA.C
  N2: LED_A_D1.anode, RA.Pin_1
  N3: LED_K_D1.cathode, QK.C
  N4: LED_K_D1.anode, RK.Pin_1
  N5: LED_B_D1.cathode, QB.C
  N6: LED_B_D1.anode, RB.Pin_1
  N7: LED_E_D1.cathode, QE.C
  N8: LED_E_D1.anode, RE.Pin_1
  N9: LED_G_D1.cathode, QG.C
  N10: LED_G_D1.anode, RG.Pin_1
  N11: LED_H_D1.cathode, QH.C
  N12: LED_H_D1.anode, RH.Pin_1
  N13: LED_N_D1.cathode, QN.C
  N14: LED_N_D1.anode, RN.Pin_1
  N15: LED_L_D1.cathode, QL.C
  N16: LED_L_D1.anode, RL.Pin_1
  N17: LED_D_D1.cathode, QD.C
  N18: LED_D_D1.anode, RD.Pin_1
  N19: LED_F_D1.cathode, QF.C
  N20: LED_F_D1.anode, RF.Pin_1
  N21: LED_I_D1.cathode, QI.C
  N22: LED_I_D1.anode, RI.Pin_1
  N23: LED_J_D1.cathode, QJ.C
  N24: LED_J_D1.anode, RJ.Pin_1
  N25: LED_C_D1.cathode, QC.C
  N26: LED_C_D1.anode, RC.Pin_1
  N27: LED_M_D1.cathode, QM.C
  N28: LED_M_D1.anode, RM.Pin_1
  5V: RA.Pin_0, RK.Pin_0, RM.Pin_0, RN.Pin_0, RG.Pin_0, RL.Pin_0, RI.Pin_0, RC.Pin_0, RF.Pin_0, RB.Pin_0, RJ.Pin_0, RH.Pin_0, RE.Pin_0, RD.Pin_0, R_up.Pin_0, R_down.Pin_0, Power.pin1
  N29: QA.E, QK.E, QI.E, QF.E, QC.E, QB.E, QH.E, QN.E, QL.E, QE.E, QD.E, QJ.E, QG.E, QM.E, Qout.C, Q.E
  N30: QA.B, RAQ.Pin_1
  N31: QK.B, RKQ.Pin_1
  N32: QI.B, RIQ.Pin_1
  N33: QF.B, RFQ.Pin_1
  N34: QC.B, RCQ.Pin_1
  N35: QB.B, RBQ.Pin_1
  N36: QH.B, RHQ.Pin_1
  N37: QN.B, RNQ.Pin_1
  N38: QL.B, RLQ.Pin_1
  N39: QE.B, REQ.Pin_1
  N40: QD.B, RDQ.Pin_1
  N41: QJ.B, RJQ.Pin_1
  N42: QG.B, RGQ.Pin_1
  N43: QM.B, RMQ.Pin_1
  sA: RAQ.Pin_0, Segments.pin1
  sF: RFQ.Pin_0, Segments.pin2
  sM: RMQ.Pin_0, Segments.pin11
  sC: RCQ.Pin_0, Segments.pin9
  sB: RBQ.Pin_0, Segments.pin6
  sJ: RJQ.Pin_0, Segments.pin4
  sE: REQ.Pin_0, Segments.pin13
  sK: RKQ.Pin_0, Segments.pin5
  sG: RGQ.Pin_0, Segments.pin8
  sH: RHQ.Pin_0, Segments.pin7
  sI: RIQ.Pin_0, Segments.pin3
  sL: RLQ.Pin_0, Segments.pin12
  GND: Qout.E, Power.pin2
  N44: Qout.B, RoutQ.Pin_1
  select: RoutQ.Pin_0, select.pin1
  sD: RDQ.Pin_0, Segments.pin14
  N45: LED__up.cathode, Q.C, LED__down.cathode
  N46: LED__up.anode, R_up.Pin_1
  N47: Q.B, R_Q.Pin_1
  s:: R_Q.Pin_0, Segments.pin15
  N48: R_down.Pin_1, LED__down.anode
  sN: RNQ.Pin_0, Segments.pin10

notes:
  These inputs should come from a 5V-based microcontroller (untested with 3.3V or others)
