# Fritzing sketch 14 segment digit (saved by Fritzing 0.9.3b)
circuit board: 8.46667cm x 6.2cm
perfboards: 1

parts:
  A = LED - 5mm [color="Red (633nm)" package="5 mm [THT]"]
  E = LED - 5mm [color="Red (633nm)" package="5 mm [THT]"]
  D = LED - 5mm [color="Red (633nm)" package="5 mm [THT]"]
  C = LED - 5mm [color="Red (633nm)" package="5 mm [THT]"]
  B = LED - 5mm [color="Red (633nm)" package="5 mm [THT]"]
  F = LED - 5mm [color="Red (633nm)" package="5 mm [THT]"]
  G = LED - 5mm [color="Red (633nm)" package="5 mm [THT]"]
  H = LED - 5mm [color="Red (633nm)" package="5 mm [THT]"]
  I = LED - 5mm [color="Red (633nm)" package="5 mm [THT]"]
  K = LED - 5mm [color="Red (633nm)" package="5 mm [THT]"]
  L = LED - 5mm [color="Red (633nm)" package="5 mm [THT]"]
  N = LED - 5mm [color="Red (633nm)" package="5 mm [THT]"]
  J = LED - 5mm [color="Red (633nm)" package="5 mm [THT]"]
  M = LED - 5mm [color="Red (633nm)" package="5 mm [THT]"]
  RA = Resistor [tolerance=±5% resistance=180 package=THT]
  RA1 = Resistor [tolerance=±5% resistance=180 package=THT]
  RA2 = Resistor [tolerance=±5% resistance=180 package=THT]
  RA3 = Resistor [tolerance=±5% resistance=180 package=THT]
  RA4 = Resistor [tolerance=±5% resistance=180 package=THT]
  RA5 = Resistor [tolerance=±5% resistance=180 package=THT]
  RA6 = Resistor [tolerance=±5% resistance=180 package=THT]
  RA7 = Resistor [tolerance=±5% resistance=180 package=THT]
  RA8 = Resistor [tolerance=±5% resistance=180 package=THT]
  RA9 = Resistor [tolerance=±5% resistance=180 package=THT]
  Q1 = NPN-Transistor [package="TO92 [THT]"]
  RA10 = Resistor [tolerance=±5% resistance=180 package=THT]
  RA11 = Resistor [tolerance=±5% resistance=180 package=THT]
  RA12 = Resistor [tolerance=±5% resistance=180 package=THT]
  RA13 = Resistor [tolerance=±5% resistance=180 package=THT]
  RA14 = Resistor [tolerance=±5% resistance=180 package=THT]
  M1 = LED - 5mm [color="Red (633nm)" package="5 mm [THT]"]
  J2 = LED - 5mm [color="Red (633nm)" package="5 mm [THT]"]
  N1 = LED - 5mm [color="Red (633nm)" package="5 mm [THT]"]
  L1 = LED - 5mm [color="Red (633nm)" package="5 mm [THT]"]
  K1 = LED - 5mm [color="Red (633nm)" package="5 mm [THT]"]
  I1 = LED - 5mm [color="Red (633nm)" package="5 mm [THT]"]
  H1 = LED - 5mm [color="Red (633nm)" package="5 mm [THT]"]
  G1 = LED - 5mm [color="Red (633nm)" package="5 mm [THT]"]
  F1 = LED - 5mm [color="Red (633nm)" package="5 mm [THT]"]
  B1 = LED - 5mm [color="Red (633nm)" package="5 mm [THT]"]
  C1 = LED - 5mm [color="Red (633nm)" package="5 mm [THT]"]
  D1 = LED - 5mm [color="Red (633nm)" package="5 mm [THT]"]
  E1 = LED - 5mm [color="Red (633nm)" package="5 mm [THT]"]
  A1 = LED - 5mm [color="Red (633nm)" package="5 mm [THT]"]
  J3 = female pin header, 16 pins [form="♀ (female)"]
  RA15 = Resistor [tolerance=±5% resistance=180 package=THT]
  RA16 = Resistor [tolerance=±5% resistance=180 package=THT]
  RA17 = Resistor [tolerance=±5% resistance=180 package=THT]
  RA18 = Resistor [tolerance=±5% resistance=180 package=THT]
  RA19 = Resistor [tolerance=±5% resistance=180 package=THT]
  RA20 = Resistor [tolerance=±5% resistance=180 package=THT]
  RA21 = Resistor [tolerance=±5% resistance=180 package=THT]
  RA22 = Resistor [tolerance=±5% resistance=180 package=THT]
  RA23 = Resistor [tolerance=±5% resistance=180 package=THT]
  RA24 = Resistor [tolerance=±5% resistance=180 package=THT]
  RA25 = Resistor [tolerance=±5% resistance=180 package=THT]
  RA26 = Resistor [tolerance=±5% resistance=180 package=THT]
  RA27 = Resistor [tolerance=±5% resistance=180 package=THT]
  RA28 = Resistor [tolerance=±5% resistance=180 package=THT]
  RA29 = Resistor [tolerance=±5% resistance=180 package=THT]
  Q2 = NPN-Transistor [package="TO92 [THT]"]
  J1 = female pin header, 16 pins [form="♀ (female)"]

nets:
  N1: A.cathode, E.cathode, D.cathode, F.cathode, G.cathode, H.cathode, J.cathode, M.cathode, RA1.Pin_0, RA4.Pin_1, RA5.Pin_0, RA7.Pin_0, Q1.C, RA12.Pin_0, RA13.Pin_0
  N2: A.anode, RA.Pin_0
  N3: E.anode, RA11.Pin_1
  N4: D.anode, RA2.Pin_0
  N5: C.cathode, RA12.Pin_1
  N6: C.anode, J1.pin14
  N7: B.cathode, RA4.Pin_0
  N8: B.anode, J1.pin3
  N9: F.anode, RA3.Pin_1
  N10: G.anode, RA8.Pin_0
  N11: H.anode, RA9.Pin_0
  N12: I.cathode, RA7.Pin_1
  N13: I.anode, J1.pin6
  N14: K.cathode, RA5.Pin_1
  N15: K.anode, J1.pin4
  N16: L.cathode, RA1.Pin_1
  N17: L.anode, J1.pin11
  N18: N.cathode, RA13.Pin_1
  N19: N.anode, J1.pin13
  N20: J.anode, RA6.Pin_0
  N21: M.anode, RA14.Pin_1
  N22: RA.Pin_1, J1.pin1
  N23: RA2.Pin_1, J1.pin16
  N24: RA3.Pin_0, J1.pin2
  N25: RA6.Pin_1, J1.pin5
  N26: RA8.Pin_1, J1.pin7
  N27: RA9.Pin_1, J1.pin8
  N28: Q1.E, J1.pin10
  N29: Q1.B, RA10.Pin_1
  N30: RA10.Pin_0, J1.pin9
  N31: RA11.Pin_0, J1.pin15
  N32: RA14.Pin_0, J1.pin12
  N33: M1.cathode, J2.cathode, H1.cathode, G1.cathode, F1.cathode, D1.cathode, E1.cathode, A1.cathode, RA16.Pin_0, RA17.Pin_0, RA22.Pin_0, RA24.Pin_1, RA25.Pin_1, RA28.Pin_1, Q2.C
  N34: M1.anode, RA15.Pin_1
  N35: J2.anode, RA23.Pin_0
  N36: N1.cathode, RA16.Pin_1
  N37: N1.anode, J3.pin13
  N38: L1.cathode, RA28.Pin_0
  N39: L1.anode, J3.pin11
  N40: K1.cathode, RA24.Pin_0
  N41: K1.anode, J3.pin4
  N42: I1.cathode, RA22.Pin_1
  N43: I1.anode, J3.pin6
  N44: H1.anode, RA20.Pin_0
  N45: G1.anode, RA21.Pin_0
  N46: F1.anode, RA26.Pin_1
  N47: B1.cathode, RA25.Pin_0
  N48: B1.anode, J3.pin3
  N49: C1.cathode, RA17.Pin_1
  N50: C1.anode, J3.pin14
  N51: D1.anode, RA27.Pin_0
  N52: E1.anode, RA18.Pin_1
  N53: A1.anode, RA29.Pin_0
  N54: J3.pin1, RA29.Pin_1
  N55: J3.pin2, RA26.Pin_0
  N56: J3.pin5, RA23.Pin_1
  N57: J3.pin7, RA21.Pin_1
  N58: J3.pin8, RA20.Pin_1
  N59: J3.pin9, RA19.Pin_0
  N60: J3.pin10, Q2.E
  N61: J3.pin12, RA15.Pin_0
  N62: J3.pin15, RA18.Pin_0
  N63: J3.pin16, RA27.Pin_1
  N64: RA19.Pin_1, Q2.B
