# Fritzing sketch daclack control (saved by Fritzing 0.9.3b)
circuit board: 8.41009cm x 6.12536cm
breadboards: 1

parts:
  ShR_2 = 74HC595 [package="DIP16 [THT]"]
  J3 = male pin header, 7 pins [form="♂ (male)"]
  Part2 = Arduino Pro Mini v13
  Part4 = Bluetooth HC-05 Macho
  R1 = Resistor [tolerance=±5% resistance=1.5k package=THT]
  R2 = Resistor [tolerance=±5% resistance=1k package=THT]
  R3 = Resistor [tolerance=±5% resistance=1.5k package=THT]
  ShR_1 = 74HC595 [package="DIP16 [THT]"]
  J6 = Power Jack [package=power_jack_slot]
  U3 = SWITCH-SPST-2 [package=switch-spst-vertical]
  Segments = female pin header, 16 pins [form="♀ (female)"]
  Seconds = male pin header, 2 pins [form="♂ (male)"]

nets:
  G: ShR_2.Q1, Segments.pin7
  I: ShR_2.Q2, Segments.pin6
  J: ShR_2.Q3, Segments.pin5
  K: ShR_2.Q4, Segments.pin4
  B: ShR_2.Q5, Segments.pin3
  F: ShR_2.Q6, Segments.pin2
  A: ShR_2.Q7, Segments.pin1
  GND: ShR_2.GND, ShR_2.OE, J3.pin3, Part2.GND, Part4.GND, R3.Pin_0, ShR_1.GND, ShR_1.OE, J6.GNDBREAK, J6.GND, Segments.pin10, Seconds.pin2
  5V: ShR_2.MR, ShR_2.VCC, Part2.VCC, Part4.VCC, ShR_1.MR, ShR_1.VCC, U3.P
  N1: ShR_2.SH_CP, Part2.D3_PWM, ShR_1.SH_CP
  N2: ShR_2.ST_CP, Part2.D6_PWM, ShR_1.ST_CP
  N3: ShR_2.DS, ShR_1.Q7'
  N4: J3.pin1, Part2.D9_PWM
  N5: J3.pin2, Part2.D8
  N6: J3.pin4, Part2.D13/SCK
  N7: J3.pin5, Part2.D12/MISO
  N8: J3.pin6, Part2.D11_PWM/MOSI
  N9: J3.pin7, Part2.D10_PWM/SS
  N10: Part2.D5_PWM, Part4.TXD
  N11: Part2.D4, R2.Pin_1
  N12: Part2.D2, ShR_1.DS
  N13: Part4.RXD, R1.Pin_1, R2.Pin_0
  N14: R1.Pin_0, R3.Pin_1
  D: ShR_1.Q1, Segments.pin16
  E: ShR_1.Q2, Segments.pin15
  C: ShR_1.Q3, Segments.pin14
  N15: ShR_1.Q4, Segments.pin13
  M: ShR_1.Q5, Segments.pin12
  L: ShR_1.Q6, Segments.pin11
  H: ShR_1.Q7, Segments.pin8
  N16: ShR_1.Q0, Seconds.pin1
  N17: J6.PWR, U3.O

notes:
  AFBKJIGHLMNCED
